// Logisim project game_of_life.circ as structural Verilog: 3 circuits, main circuit main
module main (
  input  in_1,
  input  in_2,
  input  in_3,
  input  in_4,
  input  in_5,
  input  in_6,
  input  in_7,
  input  in_8,
  input  RESET,
  input  in_10,
  input  in_11,
  input  in_12,
  input  in_13,
  input  in_14,
  input  in_15,
  input  in_16,
  input  in_17,
  input  in_18,
  input  in_19,
  input  in_20,
  input  in_21,
  input  in_22,
  input  in_23,
  input  in_24,
  input  in_25,
  input  in_26,
  input  in_27,
  input  in_28,
  input  in_29,
  input  in_30,
  input  in_31,
  input  in_32,
  input  in_33,
  input  in_34,
  input  in_35,
  input  in_36,
  input  in_37,
  input  in_38,
  input  in_39,
  input  in_40,
  input  in_41,
  input  in_42,
  input  in_43,
  input  in_44,
  input  in_45,
  input  in_46,
  input  in_47,
  input  in_48,
  input  in_49,
  input  in_50,
  input  in_51,
  input  in_52,
  input  in_53,
  input  in_54,
  input  in_55,
  input  in_56,
  input  in_57,
  input  in_58,
  input  in_59,
  input  in_60,
  input  in_61,
  input  in_62,
  input  in_63,
  input  in_64,
  input  in_65
);

  wire C11, C12, C13, C14, C15, C16, C17, C18, C21, C22, C23, C24, C25, C26, C27, C28, C31, C32, C33, C34,
       C35, C36, C37, C38, C41, C42, C43, C44, C45, C46, C47, C48, C51, C52, C53, C54, C55, C56, C57, C58,
       C61, C62, C63, C64, C65, C66, C67, C68, C71, C72, C73, C74, C75, C76, C77, C78, C81, C82, C83, C84,
       C85, C86, C87, C88, CLK;

  Clock clock_1 (.out(CLK));
  game_of_life_cell game_of_life_cell_1 (
    .SET(in_1), .CLK(CLK), .RST(RESET), .NW(C88), .N(C81), .NE(C82), .W(C18), .E(C12), .SW(C28), .S(C21),
    .SE(C22), .D(C11));
  game_of_life_cell game_of_life_cell_2 (
    .SET(in_10), .CLK(CLK), .RST(RESET), .NW(C18), .N(C11), .NE(C12), .W(C28), .E(C22), .SW(C38), .S(C31),
    .SE(C32), .D(C21));
  game_of_life_cell game_of_life_cell_3 (
    .SET(in_18), .CLK(CLK), .RST(RESET), .NW(C28), .N(C21), .NE(C22), .W(C38), .E(C32), .SW(C48), .S(C41),
    .SE(C42), .D(C31));
  game_of_life_cell game_of_life_cell_4 (
    .SET(in_26), .CLK(CLK), .RST(RESET), .NW(C38), .N(C31), .NE(C32), .W(C48), .E(C42), .SW(C58), .S(C51),
    .SE(C52), .D(C41));
  game_of_life_cell game_of_life_cell_5 (
    .SET(in_34), .CLK(CLK), .RST(RESET), .NW(C48), .N(C41), .NE(C42), .W(C58), .E(C52), .SW(C68), .S(C61),
    .SE(C62), .D(C51));
  game_of_life_cell game_of_life_cell_6 (
    .SET(in_42), .CLK(CLK), .RST(RESET), .NW(C58), .N(C51), .NE(C52), .W(C68), .E(C62), .SW(C78), .S(C71),
    .SE(C72), .D(C61));
  game_of_life_cell game_of_life_cell_7 (
    .SET(in_50), .CLK(CLK), .RST(RESET), .NW(C68), .N(C61), .NE(C62), .W(C78), .E(C72), .SW(C88), .S(C81),
    .SE(C82), .D(C71));
  game_of_life_cell game_of_life_cell_8 (
    .SET(in_58), .CLK(CLK), .RST(RESET), .NW(C78), .N(C71), .NE(C72), .W(C88), .E(C82), .SW(C18), .S(C11),
    .SE(C12), .D(C81));
  game_of_life_cell game_of_life_cell_9 (
    .SET(in_2), .CLK(CLK), .RST(RESET), .NW(C81), .N(C82), .NE(C83), .W(C11), .E(C13), .SW(C21), .S(C22),
    .SE(C23), .D(C12));
  game_of_life_cell game_of_life_cell_10 (
    .SET(in_11), .CLK(CLK), .RST(RESET), .NW(C11), .N(C12), .NE(C13), .W(C21), .E(C23), .SW(C31), .S(C32),
    .SE(C33), .D(C22));
  game_of_life_cell game_of_life_cell_11 (
    .SET(in_19), .CLK(CLK), .RST(RESET), .NW(C21), .N(C22), .NE(C23), .W(C31), .E(C33), .SW(C41), .S(C42),
    .SE(C43), .D(C32));
  game_of_life_cell game_of_life_cell_12 (
    .SET(in_27), .CLK(CLK), .RST(RESET), .NW(C31), .N(C32), .NE(C33), .W(C41), .E(C43), .SW(C51), .S(C52),
    .SE(C53), .D(C42));
  game_of_life_cell game_of_life_cell_13 (
    .SET(in_35), .CLK(CLK), .RST(RESET), .NW(C41), .N(C42), .NE(C43), .W(C51), .E(C53), .SW(C61), .S(C62),
    .SE(C63), .D(C52));
  game_of_life_cell game_of_life_cell_14 (
    .SET(in_43), .CLK(CLK), .RST(RESET), .NW(C51), .N(C52), .NE(C53), .W(C61), .E(C63), .SW(C71), .S(C72),
    .SE(C73), .D(C62));
  game_of_life_cell game_of_life_cell_15 (
    .SET(in_51), .CLK(CLK), .RST(RESET), .NW(C61), .N(C62), .NE(C63), .W(C71), .E(C73), .SW(C81), .S(C82),
    .SE(C83), .D(C72));
  game_of_life_cell game_of_life_cell_16 (
    .SET(in_59), .CLK(CLK), .RST(RESET), .NW(C71), .N(C72), .NE(C73), .W(C81), .E(C83), .SW(C11), .S(C12),
    .SE(C13), .D(C82));
  game_of_life_cell game_of_life_cell_17 (
    .SET(in_3), .CLK(CLK), .RST(RESET), .NW(C82), .N(C83), .NE(C84), .W(C12), .E(C14), .SW(C22), .S(C23),
    .SE(C24), .D(C13));
  game_of_life_cell game_of_life_cell_18 (
    .SET(in_12), .CLK(CLK), .RST(RESET), .NW(C12), .N(C13), .NE(C14), .W(C22), .E(C24), .SW(C32), .S(C33),
    .SE(C34), .D(C23));
  game_of_life_cell game_of_life_cell_19 (
    .SET(in_20), .CLK(CLK), .RST(RESET), .NW(C22), .N(C23), .NE(C24), .W(C32), .E(C34), .SW(C42), .S(C43),
    .SE(C44), .D(C33));
  game_of_life_cell game_of_life_cell_20 (
    .SET(in_28), .CLK(CLK), .RST(RESET), .NW(C32), .N(C33), .NE(C34), .W(C42), .E(C44), .SW(C52), .S(C53),
    .SE(C54), .D(C43));
  game_of_life_cell game_of_life_cell_21 (
    .SET(in_36), .CLK(CLK), .RST(RESET), .NW(C42), .N(C43), .NE(C44), .W(C52), .E(C54), .SW(C62), .S(C63),
    .SE(C64), .D(C53));
  game_of_life_cell game_of_life_cell_22 (
    .SET(in_44), .CLK(CLK), .RST(RESET), .NW(C52), .N(C53), .NE(C54), .W(C62), .E(C64), .SW(C72), .S(C73),
    .SE(C74), .D(C63));
  game_of_life_cell game_of_life_cell_23 (
    .SET(in_52), .CLK(CLK), .RST(RESET), .NW(C62), .N(C63), .NE(C64), .W(C72), .E(C74), .SW(C82), .S(C83),
    .SE(C84), .D(C73));
  game_of_life_cell game_of_life_cell_24 (
    .SET(in_60), .CLK(CLK), .RST(RESET), .NW(C72), .N(C73), .NE(C74), .W(C82), .E(C84), .SW(C12), .S(C13),
    .SE(C14), .D(C83));
  LED led_1 (.in(C11));
  LED led_2 (.in(C21));
  LED led_3 (.in(C31));
  LED led_4 (.in(C41));
  LED led_5 (.in(C51));
  LED led_6 (.in(C61));
  LED led_7 (.in(C71));
  LED led_8 (.in(C81));
  LED led_9 (.in(C12));
  LED led_10 (.in(C22));
  LED led_11 (.in(C32));
  LED led_12 (.in(C42));
  LED led_13 (.in(C52));
  LED led_14 (.in(C62));
  LED led_15 (.in(C72));
  LED led_16 (.in(C82));
  LED led_17 (.in(C13));
  LED led_18 (.in(C23));
  LED led_19 (.in(C33));
  LED led_20 (.in(C43));
  LED led_21 (.in(C53));
  LED led_22 (.in(C63));
  LED led_23 (.in(C73));
  LED led_24 (.in(C83));
  game_of_life_cell game_of_life_cell_25 (
    .SET(in_4), .CLK(CLK), .RST(RESET), .NW(C83), .N(C84), .NE(C85), .W(C13), .E(C15), .SW(C23), .S(C24),
    .SE(C25), .D(C14));
  game_of_life_cell game_of_life_cell_26 (
    .SET(in_13), .CLK(CLK), .RST(RESET), .NW(C13), .N(C14), .NE(C15), .W(C23), .E(C25), .SW(C33), .S(C34),
    .SE(C35), .D(C24));
  game_of_life_cell game_of_life_cell_27 (
    .SET(in_21), .CLK(CLK), .RST(RESET), .NW(C23), .N(C24), .NE(C25), .W(C33), .E(C35), .SW(C43), .S(C44),
    .SE(C45), .D(C34));
  game_of_life_cell game_of_life_cell_28 (
    .SET(in_29), .CLK(CLK), .RST(RESET), .NW(C33), .N(C34), .NE(C35), .W(C43), .E(C45), .SW(C53), .S(C54),
    .SE(C55), .D(C44));
  game_of_life_cell game_of_life_cell_29 (
    .SET(in_37), .CLK(CLK), .RST(RESET), .NW(C43), .N(C44), .NE(C45), .W(C53), .E(C55), .SW(C63), .S(C64),
    .SE(C65), .D(C54));
  game_of_life_cell game_of_life_cell_30 (
    .SET(in_45), .CLK(CLK), .RST(RESET), .NW(C53), .N(C54), .NE(C55), .W(C63), .E(C65), .SW(C73), .S(C74),
    .SE(C75), .D(C64));
  game_of_life_cell game_of_life_cell_31 (
    .SET(in_53), .CLK(CLK), .RST(RESET), .NW(C63), .N(C64), .NE(C65), .W(C73), .E(C75), .SW(C83), .S(C84),
    .SE(C85), .D(C74));
  game_of_life_cell game_of_life_cell_32 (
    .SET(in_61), .CLK(CLK), .RST(RESET), .NW(C73), .N(C74), .NE(C75), .W(C83), .E(C85), .SW(C13), .S(C14),
    .SE(C15), .D(C84));
  LED led_25 (.in(C14));
  LED led_26 (.in(C15));
  LED led_27 (.in(C24));
  LED led_28 (.in(C25));
  LED led_29 (.in(C34));
  LED led_30 (.in(C35));
  LED led_31 (.in(C44));
  LED led_32 (.in(C45));
  LED led_33 (.in(C54));
  LED led_34 (.in(C55));
  LED led_35 (.in(C64));
  LED led_36 (.in(C65));
  LED led_37 (.in(C74));
  LED led_38 (.in(C75));
  LED led_39 (.in(C84));
  LED led_40 (.in(C85));
  LED led_41 (.in(C16));
  LED led_42 (.in(C26));
  LED led_43 (.in(C35));
  LED led_44 (.in(C46));
  LED led_45 (.in(C56));
  LED led_46 (.in(C66));
  LED led_47 (.in(C76));
  LED led_48 (.in(C86));
  LED led_49 (.in(C17));
  LED led_50 (.in(C27));
  LED led_51 (.in(C36));
  LED led_52 (.in(C47));
  LED led_53 (.in(C57));
  LED led_54 (.in(C67));
  LED led_55 (.in(C77));
  LED led_56 (.in(C87));
  LED led_57 (.in(C18));
  LED led_58 (.in(C28));
  LED led_59 (.in(C37));
  LED led_60 (.in(C48));
  LED led_61 (.in(C58));
  LED led_62 (.in(C68));
  LED led_63 (.in(C78));
  LED led_64 (.in(C88));
  game_of_life_cell game_of_life_cell_33 (
    .SET(in_5), .CLK(CLK), .RST(RESET), .NW(C84), .N(C85), .NE(C86), .W(C14), .E(C12), .SW(C24), .S(C25),
    .SE(C26), .D(C15));
  game_of_life_cell game_of_life_cell_34 (
    .SET(in_14), .CLK(CLK), .RST(RESET), .NW(C14), .N(C15), .NE(C16), .W(C24), .E(C26), .SW(C34), .S(C35),
    .SE(C36), .D(C25));
  game_of_life_cell game_of_life_cell_35 (
    .SET(in_22), .CLK(CLK), .RST(RESET), .NW(C24), .N(C25), .NE(C26), .W(C34), .E(C36), .SW(C44), .S(C45),
    .SE(C46), .D(C35));
  game_of_life_cell game_of_life_cell_36 (
    .SET(in_30), .CLK(CLK), .RST(RESET), .NW(C34), .N(C35), .NE(C36), .W(C44), .E(C46), .SW(C54), .S(C55),
    .SE(C56), .D(C45));
  game_of_life_cell game_of_life_cell_37 (
    .SET(in_38), .CLK(CLK), .RST(RESET), .NW(C44), .N(C45), .NE(C46), .W(C54), .E(C56), .SW(C64), .S(C65),
    .SE(C66), .D(C55));
  game_of_life_cell game_of_life_cell_38 (
    .SET(in_46), .CLK(CLK), .RST(RESET), .NW(C54), .N(C55), .NE(C56), .W(C64), .E(C66), .SW(C74), .S(C75),
    .SE(C76), .D(C65));
  game_of_life_cell game_of_life_cell_39 (
    .SET(in_54), .CLK(CLK), .RST(RESET), .NW(C64), .N(C65), .NE(C66), .W(C74), .E(C76), .SW(C84), .S(C85),
    .SE(C86), .D(C75));
  game_of_life_cell game_of_life_cell_40 (
    .SET(in_62), .CLK(CLK), .RST(RESET), .NW(C74), .N(C75), .NE(C76), .W(C84), .E(C86), .SW(C14), .S(C15),
    .SE(C16), .D(C85));
  game_of_life_cell game_of_life_cell_41 (
    .SET(in_6), .CLK(CLK), .RST(RESET), .NW(C85), .N(C86), .NE(C87), .W(C15), .E(C17), .SW(C25), .S(C26),
    .SE(C27), .D(C16));
  game_of_life_cell game_of_life_cell_42 (
    .SET(in_15), .CLK(CLK), .RST(RESET), .NW(C15), .N(C16), .NE(C17), .W(C25), .E(C27), .SW(C35), .S(C36),
    .SE(C37), .D(C26));
  game_of_life_cell game_of_life_cell_43 (
    .SET(in_23), .CLK(CLK), .RST(RESET), .NW(C25), .N(C26), .NE(C27), .W(C35), .E(C37), .SW(C45), .S(C46),
    .SE(C47), .D(C36));
  game_of_life_cell game_of_life_cell_44 (
    .SET(in_31), .CLK(CLK), .RST(RESET), .NW(C35), .N(C36), .NE(C37), .W(C45), .E(C47), .SW(C55), .S(C56),
    .SE(C57), .D(C46));
  game_of_life_cell game_of_life_cell_45 (
    .SET(in_39), .CLK(CLK), .RST(RESET), .NW(C45), .N(C46), .NE(C47), .W(C55), .E(C57), .SW(C65), .S(C66),
    .SE(C67), .D(C56));
  game_of_life_cell game_of_life_cell_46 (
    .SET(in_47), .CLK(CLK), .RST(RESET), .NW(C55), .N(C56), .NE(C57), .W(C65), .E(C67), .SW(C75), .S(C76),
    .SE(C77), .D(C66));
  game_of_life_cell game_of_life_cell_47 (
    .SET(in_55), .CLK(CLK), .RST(RESET), .NW(C65), .N(C66), .NE(C67), .W(C75), .E(C77), .SW(C85), .S(C86),
    .SE(C87), .D(C76));
  game_of_life_cell game_of_life_cell_48 (
    .SET(in_63), .CLK(CLK), .RST(RESET), .NW(C75), .N(C76), .NE(C77), .W(C85), .E(C87), .SW(C15), .S(C16),
    .SE(C17), .D(C86));
  game_of_life_cell game_of_life_cell_49 (
    .SET(in_7), .CLK(CLK), .RST(RESET), .NW(C86), .N(C87), .NE(C88), .W(C16), .E(C18), .SW(C26), .S(C27),
    .SE(C28), .D(C17));
  game_of_life_cell game_of_life_cell_50 (
    .SET(in_16), .CLK(CLK), .RST(RESET), .NW(C16), .N(C17), .NE(C18), .W(C26), .E(C28), .SW(C36), .S(C37),
    .SE(C38), .D(C27));
  game_of_life_cell game_of_life_cell_51 (
    .SET(in_24), .CLK(CLK), .RST(RESET), .NW(C26), .N(C27), .NE(C28), .W(C36), .E(C38), .SW(C46), .S(C47),
    .SE(C48), .D(C37));
  game_of_life_cell game_of_life_cell_52 (
    .SET(in_32), .CLK(CLK), .RST(RESET), .NW(C36), .N(C37), .NE(C38), .W(C46), .E(C48), .SW(C56), .S(C57),
    .SE(C58), .D(C47));
  game_of_life_cell game_of_life_cell_53 (
    .SET(in_40), .CLK(CLK), .RST(RESET), .NW(C46), .N(C47), .NE(C48), .W(C56), .E(C58), .SW(C66), .S(C67),
    .SE(C68), .D(C57));
  game_of_life_cell game_of_life_cell_54 (
    .SET(in_48), .CLK(CLK), .RST(RESET), .NW(C56), .N(C57), .NE(C58), .W(C66), .E(C68), .SW(C76), .S(C77),
    .SE(C78), .D(C67));
  game_of_life_cell game_of_life_cell_55 (
    .SET(in_56), .CLK(CLK), .RST(RESET), .NW(C66), .N(C67), .NE(C68), .W(C76), .E(C78), .SW(C86), .S(C87),
    .SE(C88), .D(C77));
  game_of_life_cell game_of_life_cell_56 (
    .SET(in_64), .CLK(CLK), .RST(RESET), .NW(C76), .N(C77), .NE(C78), .W(C86), .E(C88), .SW(C16), .S(C17),
    .SE(C18), .D(C87));
  game_of_life_cell game_of_life_cell_57 (
    .SET(in_8), .CLK(CLK), .RST(RESET), .NW(C87), .N(C88), .NE(C81), .W(C17), .E(C11), .SW(C27), .S(C28),
    .SE(C21), .D(C18));
  game_of_life_cell game_of_life_cell_58 (
    .SET(in_17), .CLK(CLK), .RST(RESET), .NW(C17), .N(C18), .NE(C11), .W(C27), .E(C21), .SW(C37), .S(C38),
    .SE(C31), .D(C28));
  game_of_life_cell game_of_life_cell_59 (
    .SET(in_25), .CLK(CLK), .RST(RESET), .NW(C27), .N(C28), .NE(C21), .W(C37), .E(C31), .SW(C47), .S(C48),
    .SE(C41), .D(C38));
  game_of_life_cell game_of_life_cell_60 (
    .SET(in_33), .CLK(CLK), .RST(RESET), .NW(C37), .N(C38), .NE(C31), .W(C47), .E(C41), .SW(C57), .S(C58),
    .SE(C51), .D(C48));
  game_of_life_cell game_of_life_cell_61 (
    .SET(in_41), .CLK(CLK), .RST(RESET), .NW(C47), .N(C48), .NE(C41), .W(C57), .E(C51), .SW(C67), .S(C68),
    .SE(C61), .D(C58));
  game_of_life_cell game_of_life_cell_62 (
    .SET(in_49), .CLK(CLK), .RST(RESET), .NW(C57), .N(C58), .NE(C51), .W(C67), .E(C61), .SW(C77), .S(C78),
    .SE(C71), .D(C68));
  game_of_life_cell game_of_life_cell_63 (
    .SET(in_57), .CLK(CLK), .RST(RESET), .NW(C67), .N(C68), .NE(C61), .W(C77), .E(C71), .SW(C87), .S(C88),
    .SE(C81), .D(C78));
  game_of_life_cell game_of_life_cell_64 (
    .SET(in_65), .CLK(CLK), .RST(RESET), .NW(C77), .N(C78), .NE(C71), .W(C87), .E(C81), .SW(C17), .S(C18),
    .SE(C11), .D(C88));

  // Other names for the same wires on the sheet: RST = RESET
endmodule

module game_of_life_cell (
  input  SET,
  input  CLK,
  input  RST,
  input  NW,
  input  N,
  input  NE,
  input  W,
  input  E,
  input  SW,
  input  S,
  input  SE,
  output D
);

  wire and_1_out, and_2_out, comparator_1_eq, comparator_2_eq, not_1_out, or_1_out, or_2_out, register_2_q;
  wire [3:0] bitadder_1_out;

  Register #(.width(1)) register_1 (.D(or_1_out), .en(1'b1), .clk(CLK), .Q(D), .clr(RST));
  or or_1 (or_1_out, or_2_out, and_1_out);
  Register #(.width(1)) register_2 (.D(1'b1), .en(1'b1), .clk(CLK), .Q(register_2_q), .clr(RST));
  BitAdder bitadder_1 (.in0({SE, S, SW, E, W, NE, N, NW}), .out(bitadder_1_out));
  Comparator #(.width(4)) comparator_1 (.a(bitadder_1_out), .b(4'b0010), .eq(comparator_1_eq));  // open: gt, lt
  Comparator #(.width(4)) comparator_2 (.a(bitadder_1_out), .b(4'b0011), .eq(comparator_2_eq));  // open: gt, lt
  not not_1 (not_1_out, register_2_q);
  and and_1 (and_1_out, SET, not_1_out);
  and and_2 (and_2_out, D, comparator_1_eq);
  or or_2 (or_2_out, and_2_out, comparator_2_eq);
endmodule

module display (
);

  wire C11, C12, C13, C14, C21, C22, C23, C24, C31, C32, C33, C34, C41, C42, C43, C44;

  LED led_1 (.in(C11));
  LED led_2 (.in(C21));
  LED led_3 (.in(C31));
  LED led_4 (.in(C41));
  LED led_5 (.in(C12));
  LED led_6 (.in(C22));
  LED led_7 (.in(C32));
  LED led_8 (.in(C42));
  LED led_9 (.in(C13));
  LED led_10 (.in(C23));
  LED led_11 (.in(C33));
  LED led_12 (.in(C43));
  LED led_13 (.in(C14));
  LED led_14 (.in(C24));
  LED led_15 (.in(C34));
  LED led_16 (.in(C44));
endmodule
